# Fritzing sketch connections (saved by Fritzing 0.9.4)
perfboards: 1

parts:
  R1 = Resistor [tolerance=±5% resistance=6.8k package="0805 [SMD]"]
  R2 = Resistor [tolerance=±5% resistance=220 package="0805 [SMD]"]
  R3 = Resistor [tolerance=±5% resistance=1k package="0805 [SMD]"]
  R4 = Resistor [tolerance=±5% resistance=10 package="0805 [SMD]"]
  R5 = Resistor [tolerance=±5% resistance=100k package="0805 [SMD]"]
  R6 = Resistor [tolerance=±5% resistance=100k package="0805 [SMD]"]
  C1 = Ceramic Capacitor [capacitance="100 nF" package="0603 [SMD]"]
  C2 = Ceramic Capacitor [capacitance="100 nF" package="0603 [SMD]"]
  Q1 = TRANSISTOR_NPN_BC547 [package=to-92-ammo]
  J1 = screw terminal, 3 pins
  J2 = Screw terminal - 2 pins [package=THT]
  D3 = Schottky Diode [part_number=1N5817 package="300 mil [THT]"]
  D4 = Zener Diode [part_number=1N4732A breakdown_voltage=3.3V package="Melf DO-213 AB [SMD]"]

nets:
  N1: R1.0, Q1.C, J1.pin2
  N2: R1.1, J1.pin1
  N3: R2.0, R3.1, D4.cathode
  N4: R2.1, Q1.B
  N5: R3.0, R4.1, D3.cathode
  N6: R4.0, R5.1, C2.0
  N7: R5.0, C1.0, Q1.E, J1.pin3, D3.anode, D4.anode
  N8: R6.0, C1.1, J2.pin2
  N9: R6.1, C2.1

custom parts:
  220 Ω Resistor: A generic resistor
  Ceramic Capacitor: 0.01 nF multilayered Ceramic Capacitor
  TRANSISTOR_NPN_BC547: Generic NPN BJT. MMBT2222 is the common NPN we use. Double check against datasheet- not all devices are the same!
